// Logisim project CPU.circ as structural Verilog: 2 circuits, main circuit PC control
module PC_control (
  input  [1:0] op,
  input  [7:0] a,
  input  [3:0] imm,
  input  [3:0] PC_old,
  output [3:0] PC_new
);

  wire and_1_out, comparator_1_eq, comparator_1_gt, comparator_1_lt, multiplexer_1_out, not_1_out, not_2_out,
       undriven, undriven_2;
  wire [3:0] adder_1_out;

  not not_1 (not_1_out, undriven_2);
  not not_2 (not_2_out, comparator_1_eq);
  Comparator comparator_1 (.a(a), .b({8{1'b0}}), .gt(comparator_1_gt), .eq(comparator_1_eq), .lt(comparator_1_lt));
  and and_1 (and_1_out, undriven, not_1_out, multiplexer_1_out);
  Multiplexer #(.select(2), .enable("false")) multiplexer_1 (
    .in0(comparator_1_eq), .in1(not_2_out), .in2(comparator_1_gt), .in3(comparator_1_lt),
    .out(multiplexer_1_out), .sel(op));
  Adder #(.width(4)) adder_1 (.a(4'b0000), .b(PC_old), .out(adder_1_out));  // open: cin, cout
  Multiplexer #(.width(4), .enable("false")) multiplexer_2 (
    .in0(adder_1_out), .in1(imm), .out(PC_new), .sel(and_1_out));
endmodule

module three_register_file (
  input  [1:0] Ra,
  input  [1:0] Rb,
  input  [7:0] d,
  input  Cir,
  input  [1:0] Rd,
  input  in_6,
  input  Ck,
  output [7:0] a,
  output [7:0] b
);

  wire demultiplexer_1_out1, demultiplexer_1_out2, demultiplexer_1_out3;
  wire [7:0] register_1_q, register_2_q, register_3_q;

  Multiplexer #(.select(2), .width(8), .enable("false")) multiplexer_1 (
    .in0({8{1'b0}}), .in1(register_1_q), .in2(register_2_q), .in3(register_3_q), .out(a), .sel(Ra));
  Register register_1 (.D(d), .Q(register_1_q), .clk(demultiplexer_1_out1), .clr(Cir));  // open: en
  Multiplexer #(.select(2), .width(8), .enable("false")) multiplexer_2 (
    .in0({8{1'b0}}), .in1(register_1_q), .in2(register_2_q), .in3(register_3_q), .out(b), .sel(Rb));
  Register register_2 (.D(d), .Q(register_2_q), .clk(demultiplexer_1_out2), .clr(Cir));  // open: en
  Demultiplexer #(.select(2), .enable("false")) demultiplexer_1 (
    .out1(demultiplexer_1_out1), .out2(demultiplexer_1_out2), .out3(demultiplexer_1_out3), .in(Ck), .sel(Rd));  // open: out0
  Register register_3 (.D(d), .Q(register_3_q), .clk(demultiplexer_1_out3), .clr(Cir));  // open: en
endmodule
