// Logisim project PC control.circ as structural Verilog: 1 circuit, main circuit main
module main (
  input  [1:0] op,
  input  [7:0] a,
  input  [3:0] imm,
  input  [3:0] PC_old,
  output [3:0] PC_new
);

  wire and_1_out, comparator_1_eq, comparator_1_gt, comparator_1_lt, multiplexer_1_out, not_1_out, not_2_out,
       undriven, undriven_2;
  wire [3:0] adder_1_out;

  Comparator comparator_1 (.a(a), .b({8{1'b0}}), .gt(comparator_1_gt), .eq(comparator_1_eq), .lt(comparator_1_lt));
  not not_1 (not_1_out, undriven_2);
  not not_2 (not_2_out, comparator_1_eq);
  and and_1 (and_1_out, undriven, not_1_out, multiplexer_1_out);
  Multiplexer #(.select(2), .enable("false")) multiplexer_1 (
    .in0(comparator_1_eq), .in1(not_2_out), .in2(comparator_1_gt), .in3(comparator_1_lt),
    .out(multiplexer_1_out), .sel(op));
  Adder #(.width(4)) adder_1 (.a(4'b0000), .b(PC_old), .out(adder_1_out));  // open: cin, cout
  Multiplexer #(.width(4), .enable("false")) multiplexer_2 (
    .in0(adder_1_out), .in1(imm), .out(PC_new), .sel(and_1_out));
endmodule
